// Logisim project smart bicycle.circ as structural Verilog: 8 circuits, main circuit Smart Bicycle
module Smart_Bicycle (
  input  Always_high,
  output LSB,
  output out_3,
  output out_4,
  output out_5,
  output out_6,
  output out_7,
  output out_8,
  output out_9,
  output out_10,
  output out_11,
  output out_12,
  output out_13,
  output MSB,
  output LSB_2,
  output out_16,
  output out_17,
  output out_18,
  output out_19,
  output out_20,
  output out_21,
  output out_22,
  output out_23
);

  wire Hall_Effect_Sensor_out, pulsegenerator_1__0_9_second_pulse_generator,
       pulsegenerator_1__1_second_pulse_generator;

  Button Hall_Effect_Sensor (.out(Hall_Effect_Sensor_out));
  pulsegenerator pulsegenerator_1 (
    .Always_High(Always_high), ._1_Second_Pulse_Generator(pulsegenerator_1__1_second_pulse_generator),
    ._0_9_Second_Pulse_Generator(pulsegenerator_1__0_9_second_pulse_generator));
  distance distance_1 (
    .Always_Connected_to_High(Always_high), .Hall_Effect_Sensor(Hall_Effect_Sensor_out), .D1(LSB),
    .D2(out_3), .D3(out_4), .D4(out_5), .D5(out_6), .D6(out_7), .D7(out_8), .D8(out_9), .D9(out_10),
    .D10(out_11), .D11(out_12), .D12(out_13), .D13(MSB));
  speed speed_1 (
    .Always_connected_to_high(Always_high), .Hall_Effect_Sensor(Hall_Effect_Sensor_out),
    ._1_second_Pulse(pulsegenerator_1__1_second_pulse_generator),
    ._0_9_second_pulse(pulsegenerator_1__0_9_second_pulse_generator), .S1(LSB_2), .S2(out_16), .S3(out_17),
    .S4(out_18), .S5(out_19), .S6(out_20), .S7(out_21), .S8(out_22), .S9(out_23));

  // Notes on the sheet:
  //   Pulse Generator
  //   1 second pulse
  //   0.9 second pulse
  //   Smart Bicycle
  //   Speed Calculator
  //   Distance Calculator
  //   Distance Output
  //   Speed Output
  //   MSB
endmodule

// Speed
module speed (
  input  Always_connected_to_high,
  input  Hall_Effect_Sensor,
  input  _1_second_Pulse,
  input  _0_9_second_pulse,
  output S1,
  output S2,
  output S3,
  output S4,
  output S5,
  output S6,
  output S7,
  output S8,
  output S9
);

  wire n9bitadder_1_o1, n9bitadder_1_o2, n9bitadder_1_o3, n9bitadder_1_o4, n9bitadder_1_o5, n9bitadder_1_o6,
       n9bitadder_1_o7, n9bitadder_1_o8, n9bitadder_1_o9, not_1_out, not_2_out, or_1_out, reset_1_o1,
       reset_1_o2, reset_1_o3, reset_1_o4, reset_1_o5, reset_1_o6, reset_1_o7, reset_1_o8, reset_1_o9,
       Sum_1_q, Sum_2_q, Sum_3_q, Sum_4_q, Sum_5_q, Sum_6_q, Sum_7_q, Sum_8_q, Sum_9_q, Updated_Sum_1_q,
       Updated_Sum_2_q, Updated_Sum_3_q, Updated_Sum_4_q, Updated_Sum_5_q, Updated_Sum_6_q, Updated_Sum_7_q,
       Updated_Sum_8_q, Updated_Sum_9_q;

  _9bitadder u_9bitadder_1 (
    .A1(Updated_Sum_1_q), .A2(Updated_Sum_2_q), .A3(Updated_Sum_3_q), .A4(Updated_Sum_4_q),
    .A5(Updated_Sum_5_q), .A6(Updated_Sum_6_q), .A7(Updated_Sum_7_q), .A8(Updated_Sum_8_q),
    .B2(Always_connected_to_high), .A9(Updated_Sum_9_q), .B5(Always_connected_to_high), .O1(n9bitadder_1_o1),
    .O2(n9bitadder_1_o2), .O3(n9bitadder_1_o3), .O4(n9bitadder_1_o4), .O5(n9bitadder_1_o5),
    .O6(n9bitadder_1_o6), .O7(n9bitadder_1_o7), .O8(n9bitadder_1_o8), .O9(n9bitadder_1_o9));
  not not_1 (not_1_out, _1_second_Pulse);
  reset reset_1 (
    .I1(n9bitadder_1_o1), .I2(n9bitadder_1_o2), .I3(n9bitadder_1_o3), .I4(n9bitadder_1_o4),
    .I5(n9bitadder_1_o5), .I6(n9bitadder_1_o6), .I7(n9bitadder_1_o7), .I8(n9bitadder_1_o8),
    .I9(n9bitadder_1_o9), .not_1_second_pulse(not_1_out), .o1(reset_1_o1), .o2(reset_1_o2), .o3(reset_1_o3),
    .o4(reset_1_o4), .o5(reset_1_o5), .o6(reset_1_o6), .o7(reset_1_o7), .o8(reset_1_o8), .o9(reset_1_o9));
  or or_1 (or_1_out, Hall_Effect_Sensor, _1_second_Pulse);
  D_Flip_Flop #(.trigger("high")) Sum_1 (.clk(or_1_out), .D(reset_1_o1), .Q(Sum_1_q));  // open: Qn, preset, en, reset
  D_Flip_Flop #(.trigger("high")) Sum_2 (.clk(or_1_out), .D(reset_1_o2), .Q(Sum_2_q));  // open: Qn, preset, en, reset
  D_Flip_Flop #(.trigger("high")) Sum_3 (.clk(or_1_out), .D(reset_1_o3), .Q(Sum_3_q));  // open: Qn, preset, en, reset
  D_Flip_Flop #(.trigger("high")) Sum_4 (.clk(or_1_out), .D(reset_1_o4), .Q(Sum_4_q));  // open: Qn, preset, en, reset
  D_Flip_Flop #(.trigger("high")) Sum_5 (.clk(or_1_out), .D(reset_1_o5), .Q(Sum_5_q));  // open: Qn, preset, en, reset
  D_Flip_Flop #(.trigger("high")) Sum_6 (.clk(or_1_out), .D(reset_1_o6), .Q(Sum_6_q));  // open: Qn, preset, en, reset
  D_Flip_Flop #(.trigger("high")) Sum_7 (.clk(or_1_out), .D(reset_1_o7), .Q(Sum_7_q));  // open: Qn, preset, en, reset
  D_Flip_Flop #(.trigger("high")) Sum_8 (.clk(or_1_out), .D(reset_1_o8), .Q(Sum_8_q));  // open: Qn, preset, en, reset
  D_Flip_Flop #(.trigger("high")) Sum_9 (.clk(or_1_out), .D(reset_1_o9), .Q(Sum_9_q));  // open: Qn, preset, en, reset
  not not_2 (not_2_out, Hall_Effect_Sensor);
  D_Flip_Flop #(.trigger("high")) Updated_Sum_1 (
    .clk(not_2_out), .D(Sum_1_q), .Q(Updated_Sum_1_q));  // open: Qn, preset, en, reset
  D_Flip_Flop #(.trigger("high")) Updated_Sum_2 (
    .clk(not_2_out), .D(Sum_2_q), .Q(Updated_Sum_2_q));  // open: Qn, preset, en, reset
  D_Flip_Flop #(.trigger("high")) Updated_Sum_3 (
    .clk(not_2_out), .D(Sum_3_q), .Q(Updated_Sum_3_q));  // open: Qn, preset, en, reset
  D_Flip_Flop #(.trigger("high")) Updated_Sum_4 (
    .clk(not_2_out), .D(Sum_4_q), .Q(Updated_Sum_4_q));  // open: Qn, preset, en, reset
  D_Flip_Flop #(.trigger("high")) Updated_Sum_5 (
    .clk(not_2_out), .D(Sum_5_q), .Q(Updated_Sum_5_q));  // open: Qn, preset, en, reset
  D_Flip_Flop #(.trigger("high")) Updated_Sum_6 (
    .clk(not_2_out), .D(Sum_6_q), .Q(Updated_Sum_6_q));  // open: Qn, preset, en, reset
  D_Flip_Flop #(.trigger("high")) Updated_Sum_7 (
    .clk(not_2_out), .D(Sum_7_q), .Q(Updated_Sum_7_q));  // open: Qn, preset, en, reset
  D_Flip_Flop #(.trigger("high")) Updated_Sum_8 (
    .clk(not_2_out), .D(Sum_8_q), .Q(Updated_Sum_8_q));  // open: Qn, preset, en, reset
  D_Flip_Flop #(.trigger("high")) Updated_Sum_9 (
    .clk(not_2_out), .D(Sum_9_q), .Q(Updated_Sum_9_q));  // open: Qn, preset, en, reset
  D_Flip_Flop #(.trigger("high")) Output_1 (
    .clk(_0_9_second_pulse), .D(Updated_Sum_1_q), .Q(S1));  // open: Qn, preset, en, reset
  D_Flip_Flop #(.trigger("high")) Output_2 (
    .clk(_0_9_second_pulse), .D(Updated_Sum_2_q), .Q(S2));  // open: Qn, preset, en, reset
  D_Flip_Flop #(.trigger("high")) Output__3 (
    .clk(_0_9_second_pulse), .D(Updated_Sum_3_q), .Q(S3));  // open: Qn, preset, en, reset
  D_Flip_Flop #(.trigger("high")) Output__4 (
    .clk(_0_9_second_pulse), .D(Updated_Sum_4_q), .Q(S4));  // open: Qn, preset, en, reset
  D_Flip_Flop #(.trigger("high")) Output_5 (
    .clk(_0_9_second_pulse), .D(Updated_Sum_5_q), .Q(S5));  // open: Qn, preset, en, reset
  D_Flip_Flop #(.trigger("high")) Output__6 (
    .clk(_0_9_second_pulse), .D(Updated_Sum_6_q), .Q(S6));  // open: Qn, preset, en, reset
  D_Flip_Flop #(.trigger("high")) Output_7 (
    .clk(_0_9_second_pulse), .D(Updated_Sum_7_q), .Q(S7));  // open: Qn, preset, en, reset
  D_Flip_Flop #(.trigger("high")) Output_8 (
    .clk(_0_9_second_pulse), .D(Updated_Sum_8_q), .Q(S8));  // open: Qn, preset, en, reset
  D_Flip_Flop #(.trigger("high")) Output_9 (
    .clk(_0_9_second_pulse), .D(Updated_Sum_9_q), .Q(S9));  // open: Qn, preset, en, reset

  // Notes on the sheet:
  //   9 bit adder
  //   Speed Calculator
  //   Reset
  //   Hidden Sum
  //   Sum Updated 
  //   Whenever Sensor is Off
  //   Output Updated
  //   Every second
  //   Binary output
  //   LSB
  //   MSB
endmodule

// Reset Everything to zero
module reset (
  input  I1,
  input  I2,
  input  I3,
  input  I4,
  input  I5,
  input  I6,
  input  I7,
  input  I8,
  input  I9,
  input  not_1_second_pulse,
  output o1,
  output o2,
  output o3,
  output o4,
  output o5,
  output o6,
  output o7,
  output o8,
  output o9
);

  and and_1 (o1, I1, not_1_second_pulse);
  and and_2 (o2, I2, not_1_second_pulse);
  and and_3 (o3, I3, not_1_second_pulse);
  and and_4 (o4, I4, not_1_second_pulse);
  and and_5 (o5, I5, not_1_second_pulse);
  and and_6 (o6, I6, not_1_second_pulse);
  and and_7 (o7, I7, not_1_second_pulse);
  and and_8 (o8, I8, not_1_second_pulse);
  and and_9 (o9, I9, not_1_second_pulse);

  // Notes on the sheet:
  //   Reseting the input to zero
endmodule

// 9 binary adding with 18
module _9bitadder (
  input  A1,
  input  A2,
  input  A3,
  input  A4,
  input  A5,
  input  A6,
  input  A7,
  input  A8,
  input  B2,
  input  A9,
  input  B5,
  output O1,
  output O2,
  output O3,
  output O4,
  output O5,
  output O6,
  output O7,
  output O8,
  output O9
);

  wire and_1_out, and_2_out, and_3_out, and_4_out, and_5_out, and_6_out, and_7_out, and_8_out, and_9_out,
       or_1_out, xor_1_out;

  xor xor_1 (xor_1_out, A5, B5);
  and and_1 (and_1_out, A5, B5);
  xor xor_2 (O6, or_1_out, A6);
  and and_2 (and_2_out, or_1_out, A6);
  xor xor_3 (O7, and_2_out, A7);
  and and_3 (and_3_out, and_2_out, A7);
  xor xor_4 (O8, and_3_out, A8);
  and and_4 (and_4_out, and_3_out, A8);
  xor xor_5 (O9, and_4_out, A9);
  and and_5 (and_5_out, and_4_out, A9);
  xor xor_6 (O2, A2, B2);
  and and_6 (and_6_out, A2, B2);
  xor xor_7 (O3, A3, and_6_out);
  and and_7 (and_7_out, A3, and_6_out);
  xor xor_8 (O4, and_7_out, A4);
  and and_8 (and_8_out, and_7_out, A4);
  xor xor_9 (O5, xor_1_out, and_8_out);
  and and_9 (and_9_out, xor_1_out, and_8_out);
  or or_1 (or_1_out, and_9_out, and_1_out);

  assign O1 = A1;

  // Notes on the sheet:
  //   9 bit Adder with 18
endmodule

// Pulse Generator
module pulsegenerator (
  input  Always_High,
  output _1_Second_Pulse_Generator,
  output _0_9_Second_Pulse_Generator
);

  wire _32Hz_clock_out, and_1_out, Counter_T_flip_flop_1_q, Counter_T_flip_flop_2_q, Counter_T_flip_flop_3_q,
       Counter_T_flip_flop_4_q, not_1_out;

  Clock _32Hz_clock (.out(_32Hz_clock_out));
  T_Flip_Flop #(.trigger("falling")) Counter_T_flip_flop_1 (
    .clk(_32Hz_clock_out), .T(Always_High), .Q(Counter_T_flip_flop_1_q));  // open: Qn, preset, reset, en
  T_Flip_Flop #(.trigger("falling")) Counter_T_flip_flop_2 (
    .clk(Counter_T_flip_flop_1_q), .T(Always_High), .Q(Counter_T_flip_flop_2_q));  // open: Qn, preset, reset, en
  T_Flip_Flop #(.trigger("falling")) Counter_T_flip_flop_3 (
    .clk(Counter_T_flip_flop_2_q), .T(Always_High), .Q(Counter_T_flip_flop_3_q));  // open: Qn, preset, reset, en
  T_Flip_Flop #(.trigger("falling")) Counter_T_flip_flop_4 (
    .clk(Counter_T_flip_flop_3_q), .T(Always_High), .Q(Counter_T_flip_flop_4_q));  // open: Qn, preset, reset, en
  and and_1 (and_1_out, Counter_T_flip_flop_4_q, Counter_T_flip_flop_3_q, Counter_T_flip_flop_1_q);
  not not_1 (not_1_out, Counter_T_flip_flop_2_q);
  and and_2 (_1_Second_Pulse_Generator, and_1_out, Counter_T_flip_flop_2_q);
  and and_3 (_0_9_Second_Pulse_Generator, and_1_out, not_1_out);

  // Notes on the sheet:
  //   Asynchronous Counter
  //   Pulse Generator
endmodule

// 13bit adder with 5
module _13adder (
  input  A1,
  input  B1,
  input  A2,
  input  A3,
  input  B3,
  input  A4,
  input  A5,
  input  A6,
  input  A7,
  input  A8,
  input  A9,
  input  A10,
  input  A11,
  input  A12,
  input  A13,
  output O1,
  output O2,
  output O3,
  output O4,
  output O5,
  output O6,
  output O7,
  output O8,
  output O9,
  output O10,
  output O11,
  output O12,
  output O13
);

  wire and_1_out, and_2_out, and_3_out, and_4_out, and_5_out, and_6_out, and_7_out, and_8_out, and_9_out,
       and_10_out, and_11_out, and_12_out, and_14_out, or_1_out, xor_1_out;

  xor xor_1 (xor_1_out, A3, B3);
  and and_1 (and_1_out, A3, B3);
  xor xor_2 (O1, A1, B1);
  and and_2 (and_2_out, B1, A1);
  xor xor_3 (O2, and_2_out, A2);
  and and_3 (and_3_out, A2, and_2_out);
  xor xor_4 (O4, or_1_out, A4);
  and and_4 (and_4_out, A4, or_1_out);
  xor xor_5 (O5, and_4_out, A5);
  and and_5 (and_5_out, A5, and_4_out);
  xor xor_6 (O6, and_5_out, A6);
  and and_6 (and_6_out, A6, and_5_out);
  xor xor_7 (O7, and_6_out, A7);
  and and_7 (and_7_out, A7, and_6_out);
  xor xor_8 (O8, and_7_out, A8);
  and and_8 (and_8_out, A8, and_7_out);
  xor xor_9 (O9, and_8_out, A9);
  and and_9 (and_9_out, A9, and_8_out);
  xor xor_10 (O10, and_9_out, A10);
  and and_10 (and_10_out, A10, and_9_out);
  xor xor_11 (O11, and_10_out, A11);
  and and_11 (and_11_out, A11, and_10_out);
  xor xor_12 (O12, and_11_out, A12);
  and and_12 (and_12_out, A12, and_11_out);
  xor xor_13 (O13, and_12_out, A13);
  // AND_Gate and_13 has open pins: in0=A13, in1=and_12_out, out=open
  xor xor_14 (O3, xor_1_out, and_3_out);
  and and_14 (and_14_out, xor_1_out, and_3_out);
  or or_1 (or_1_out, and_14_out, and_1_out);

  // Notes on the sheet:
  //   13 bit Binary adder with 5
endmodule

// Distance
module distance (
  input  Always_Connected_to_High,
  input  Hall_Effect_Sensor,
  output D1,
  output D2,
  output D3,
  output D4,
  output D5,
  output D6,
  output D7,
  output D8,
  output D9,
  output D10,
  output D11,
  output D12,
  output D13
);

  wire n13adder_1_o1, n13adder_1_o2, n13adder_1_o3, n13adder_1_o4, n13adder_1_o5, n13adder_1_o6,
       n13adder_1_o7, n13adder_1_o8, n13adder_1_o9, n13adder_1_o10, n13adder_1_o11, n13adder_1_o12,
       n13adder_1_o13, not_1_out, Sum_1_q, Sum_2_q, Sum_3_q, Sum_4_q, Sum_5_q, Sum_6_q, Sum_7_q, Sum_8_q,
       Sum_9_q, Sum_10_q, Sum_11_q, Sum_12_q, Sum_13_q;

  _13adder u_13adder_1 (
    .A1(D1), .B1(Always_Connected_to_High), .A2(D2), .A3(D3), .B3(Always_Connected_to_High), .A4(D4),
    .A5(D5), .A6(D6), .A7(D7), .A8(D8), .A9(D9), .A10(D10), .A11(D11), .A12(D12), .A13(D13),
    .O1(n13adder_1_o1), .O2(n13adder_1_o2), .O3(n13adder_1_o3), .O4(n13adder_1_o4), .O5(n13adder_1_o5),
    .O6(n13adder_1_o6), .O7(n13adder_1_o7), .O8(n13adder_1_o8), .O9(n13adder_1_o9), .O10(n13adder_1_o10),
    .O11(n13adder_1_o11), .O12(n13adder_1_o12), .O13(n13adder_1_o13));
  D_Flip_Flop #(.trigger("high")) Sum_1 (
    .clk(Hall_Effect_Sensor), .D(n13adder_1_o1), .Q(Sum_1_q));  // open: Qn, preset, en, reset
  D_Flip_Flop #(.trigger("high")) Sum_2 (
    .clk(Hall_Effect_Sensor), .D(n13adder_1_o2), .Q(Sum_2_q));  // open: Qn, preset, en, reset
  D_Flip_Flop #(.trigger("high")) Sum_3 (
    .clk(Hall_Effect_Sensor), .D(n13adder_1_o3), .Q(Sum_3_q));  // open: Qn, preset, en, reset
  D_Flip_Flop #(.trigger("high")) Sum_4 (
    .clk(Hall_Effect_Sensor), .D(n13adder_1_o4), .Q(Sum_4_q));  // open: Qn, preset, en, reset
  D_Flip_Flop #(.trigger("high")) Sum_5 (
    .clk(Hall_Effect_Sensor), .D(n13adder_1_o5), .Q(Sum_5_q));  // open: Qn, preset, en, reset
  D_Flip_Flop #(.trigger("high")) Sum_6 (
    .clk(Hall_Effect_Sensor), .D(n13adder_1_o6), .Q(Sum_6_q));  // open: Qn, preset, en, reset
  D_Flip_Flop #(.trigger("high")) Sum_7 (
    .clk(Hall_Effect_Sensor), .D(n13adder_1_o7), .Q(Sum_7_q));  // open: Qn, preset, en, reset
  D_Flip_Flop #(.trigger("high")) Sum_8 (
    .clk(Hall_Effect_Sensor), .D(n13adder_1_o8), .Q(Sum_8_q));  // open: Qn, preset, en, reset
  D_Flip_Flop #(.trigger("high")) Sum_9 (
    .clk(Hall_Effect_Sensor), .D(n13adder_1_o9), .Q(Sum_9_q));  // open: Qn, preset, en, reset
  D_Flip_Flop #(.trigger("high")) Sum_10 (
    .clk(Hall_Effect_Sensor), .D(n13adder_1_o10), .Q(Sum_10_q));  // open: Qn, preset, en, reset
  D_Flip_Flop #(.trigger("high")) Sum_11 (
    .clk(Hall_Effect_Sensor), .D(n13adder_1_o11), .Q(Sum_11_q));  // open: Qn, preset, en, reset
  D_Flip_Flop #(.trigger("high")) Sum_12 (
    .clk(Hall_Effect_Sensor), .D(n13adder_1_o12), .Q(Sum_12_q));  // open: Qn, preset, en, reset
  D_Flip_Flop #(.trigger("high")) Sum_13 (
    .clk(Hall_Effect_Sensor), .D(n13adder_1_o13), .Q(Sum_13_q));  // open: Qn, preset, en, reset
  not not_1 (not_1_out, Hall_Effect_Sensor);
  D_Flip_Flop #(.trigger("high")) Output_1 (.clk(not_1_out), .D(Sum_1_q), .Q(D1));  // open: Qn, preset, en, reset
  D_Flip_Flop #(.trigger("high")) Output_2 (.clk(not_1_out), .D(Sum_2_q), .Q(D2));  // open: Qn, preset, en, reset
  D_Flip_Flop #(.trigger("high")) Output_3 (.clk(not_1_out), .D(Sum_3_q), .Q(D3));  // open: Qn, preset, en, reset
  D_Flip_Flop #(.trigger("high")) Output_4 (.clk(not_1_out), .D(Sum_4_q), .Q(D4));  // open: Qn, preset, en, reset
  D_Flip_Flop #(.trigger("high")) Output_5 (.clk(not_1_out), .D(Sum_5_q), .Q(D5));  // open: Qn, preset, en, reset
  D_Flip_Flop #(.trigger("high")) Output_6 (.clk(not_1_out), .D(Sum_6_q), .Q(D6));  // open: Qn, preset, en, reset
  D_Flip_Flop #(.trigger("high")) Output_7 (.clk(not_1_out), .D(Sum_7_q), .Q(D7));  // open: Qn, preset, en, reset
  D_Flip_Flop #(.trigger("high")) Output_8 (.clk(not_1_out), .D(Sum_8_q), .Q(D8));  // open: Qn, preset, en, reset
  D_Flip_Flop #(.trigger("high")) Output_9 (.clk(not_1_out), .D(Sum_9_q), .Q(D9));  // open: Qn, preset, en, reset
  D_Flip_Flop #(.trigger("high")) Output_10 (.clk(not_1_out), .D(Sum_10_q), .Q(D10));  // open: Qn, preset, en, reset
  D_Flip_Flop #(.trigger("high")) Output_11 (.clk(not_1_out), .D(Sum_11_q), .Q(D11));  // open: Qn, preset, en, reset
  D_Flip_Flop #(.trigger("high")) Output_12 (.clk(not_1_out), .D(Sum_12_q), .Q(D12));  // open: Qn, preset, en, reset
  D_Flip_Flop #(.trigger("high")) Output_13 (.clk(not_1_out), .D(Sum_13_q), .Q(D13));  // open: Qn, preset, en, reset

  // Notes on the sheet:
  //   Distance Calculator
  //   13 bit Adder with 5
  //   Hidden Sum
  //   Output Sum
  //   Updated whenever Sensor is Off
  //   Output in Binary
  //   LSB
  //   MSB
endmodule

module indicator (
  input  Left_Indicator_Switch,
  input  Right_Indicator_Switch,
  input  Emergency_Lights,
  output Left_Indicator,
  output Right_Indicator
);

  wire Clock_out, or_1_out, or_2_out;

  Clock #(.highDuration(16), .lowDuration(16)) Clock (.out(Clock_out));
  or or_1 (or_1_out, Left_Indicator_Switch, Emergency_Lights);
  or or_2 (or_2_out, Emergency_Lights, Right_Indicator_Switch);
  and and_1 (Left_Indicator, Clock_out, or_1_out);
  and and_2 (Right_Indicator, Clock_out, or_2_out);

  // Notes on the sheet:
  //   Indicator System
endmodule
